# Fritzing sketch Access_Control_System_Fritzing (saved by Fritzing 0.9.3b)
breadboards: 1

parts:
  Part1 = Adafruit T-Cobbler Plus [part_number="Adafruit #1989 and #2028"]
  Componente2 = RFID-RC522-v2
  CAMERA2 = TTL Serial JPEG Camera  # not connected
  Raspberry_Pi_2 = Raspberry Pi 3 [part_number=RPI-3-V1.2]  # not connected

nets:
  +3.3V: Part1.+3.3V, Componente2.3.3V
  GND: Part1.GND, Componente2.GND
  N1: Part1.MOSI, Componente2.MOSI
  N2: Part1.MISO, Componente2.MISO
  N3: Part1.SCLK, Componente2.SCK
  N4: Part1.GPIO25, Componente2.RST
  N5: Part1.CE0, Componente2.SDA

custom parts:
  Adafruit T-Cobbler Plus: The Raspberry Pi has landed on the Maker World like a 40-GPIO pinned, quad-USB ported, credit card sized bomb of DIY joy. And while you can use most of our great Model B accessories by hooking up our downgrade cable, its probably a good time to upgrade your set up and accessorize using all of the 40 pins. That's why we now carry the Assembled Adafruit Pi T-Cobbler Plus - Breakout + Cable for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
  RFID-RC522-v2: A simple China made RFID-RC522 Reader; do check the pin labels, as this is a MFRC522 based clone.
  TTL Serial JPEG Camera: TTL Serial JPEG Camera with NTSC Out
